# Fritzing sketch arm (saved by Fritzing 0.9.3b)
breadboards: 1

parts:
  U1 = LCD-16X2 [package=lcd-16x2]
  Part1 = Arduino Mega ADK (Rev3)
  J2 = Basic Servo
  J3 = Basic Servo
  J4 = Basic Servo
  J5 = Basic Servo
  J6 = Basic Servo
  J8 = Basic Servo
  Infrared = TSOP312.., 314.. [package=THT]
  Proximity = TSOP312.., 314.. [package=THT]
  J7 = Basic Servo
  Matrix_keypad1 = KEYPAD 4x4
  L1 = Solenoid
  L2 = Solenoid
  M1 = DC Motor
  U2 = 4-Channel 5v Relay Shield [package=relay-4ch5v10a]

nets:
  N1: U1.VSS, Part1.D21/SCL
  N2: U1.VDD, Part1.D20/SDA
  GND: U1.VO, Part1.GND, J2.gnd, J3.gnd, J4.gnd, J5.gnd, J6.gnd, Infrared.GND, Proximity.GND, J7.gnd, U2.GND
  5V: U1.RS, Part1.5V, U2.VCC
  N3: Part1.A0, Infrared.Data
  N4: Part1.A1, Proximity.Data
  N5: Part1.D22, Matrix_keypad1.col1
  N6: Part1.D24, Matrix_keypad1.col2
  N7: Part1.D26, Matrix_keypad1.col3
  N8: Part1.D28, Matrix_keypad1.col4
  N9: Part1.D30, Matrix_keypad1.row1
  N10: Part1.D32, Matrix_keypad1.row2
  N11: Part1.D34, Matrix_keypad1.row3
  N12: Part1.D36, Matrix_keypad1.row4
  N13: Part1.D49, U2.IN4
  N14: Part1.D51/MOSI, U2.IN3
  N15: Part1.D53/SS, U2.IN2
  VCC: J2.vcc, J3.vcc, J4.vcc, J5.vcc, J6.vcc, J8.vcc, Infrared.Vs, Proximity.Vs, J7.vcc
  N16: L1.pin2, U2.K2-On
  N17: L2.pin2, U2.K1-On
  N18: M1.pin_1, U2.K1-Off
  N19: M1.pin_2, U2.K3-On

notes:
  5V
  12V

custom parts:
  KEYPAD 4x4: Matrix keypad 16 buttons, 4 rows x 4 columns
  4-Channel 5v Relay Shield: 4 Channel 5v Relay Shield w. 2x SPD-06VDC-SD-C
